# Fritzing sketch LDP-Wiring (saved by Fritzing 1.0.6)
breadboards: 1

parts:
  A1 = XIAO ESP32C3-smd
  U1 = Vibration Motor- ROB-08449 [package=vibe-motor-10mm]
  Q1 = NPN-Transistor [package="TO92 [THT]"]
  S1 = Round Pushbutton
  Bat1 = battery_holder_single_18650
  D1 = Rectifier Diode [part_number=1N4001 package="Melf DO-213 AB [SMD]"]
  LED1 = RGB LED (com. cathode, rbg) [color="Red (633nm)" current=0.030A package="5 mm [THT]"]
  R3 = Resistor [tolerance=±1% resistance=220k power=0.25W package=THT]
  R2 = Resistor [tolerance=±1% resistance=220k power=0.25W package=THT]
  R1 = Resistor [tolerance=±5% resistance=1k power=0.25W package=THT]

nets:
  N1: A1.Pin_2, A1.Pin_11, A1.Pin_21, Q1.C, S1.leg0, Bat1.+#0, LED1.common_cathode, R3.Pin_0
  N2: A1.Pin_8, U1.-, Bat1.+#1, D1.cathode, R2.Pin_0
  N3: A1.Pin_9, R3.Pin_1, R2.Pin_1
  N4: A1.Pin_10, S1.leg1
  N5: A1.Pin_12, LED1.green_anode
  N6: A1.Pin_13, LED1.blue_anode
  N7: A1.Pin_14, LED1.red_anode
  N8: A1.Pin_19, R1.Pin_1
  N9: U1.+, Q1.E, D1.anode
  N10: Q1.B, R1.Pin_0

notes:
  3.3v
  GND
  D10
  D2
  COM
  NO
  D0
  1k
  220k
  17 (edge)

custom parts:
  XIAO ESP32C3-smd: Seeed Studio XIAO ESP32C3 adopts new RISC-V architecture, supporting both Wi-Fi and BLE wireless connectivities.
  battery_holder_single_18650: single 18650 battery holder
