# Fritzing sketch circuit schematic (saved by Fritzing 1.0.6)
breadboards: 1

parts:
  A1 = XIAO ESP32C3-smd
  U1 = Vibration Motor- ROB-08449 [package=vibe-motor-10mm]
  R1 = Resistor [tolerance=±5% resistance=1k package="2010 [SMD]"]
  Q1 = NPN-Transistor [package="TO92 [THT]"]
  S1 = Round Pushbutton
  Bat1 = battery_holder_single_18650
  R2 = Resistor [tolerance=±5% resistance=220k package="2010 [SMD]"]
  R3 = Resistor [tolerance=±5% resistance=220k package="2010 [SMD]"]
  D1 = Rectifier Diode [part_number=1N4001 package="Melf DO-213 AB [SMD]"]

nets:
  N1: A1.Pin_2, A1.Pin_18, A1.Pin_21, Q1.C, S1.leg1, Bat1.+#0, R3.Pin_0
  N2: A1.Pin_8, U1.-, R2.Pin_0, D1.cathode
  N3: A1.Pin_9, R2.Pin_1, R3.Pin_1
  N4: A1.Pin_11, S1.leg0
  N5: A1.Pin_19, R1.Pin_1, Bat1.+#1
  N6: U1.+, Q1.E, D1.anode
  N7: R1.Pin_0, Q1.B

notes:
  3.3v
  GND
  D10
  D2
  COM
  NO
  D0

custom parts:
  XIAO ESP32C3-smd: Seeed Studio XIAO ESP32C3 adopts new RISC-V architecture, supporting both Wi-Fi and BLE wireless connectivities.
  battery_holder_single_18650: single 18650 battery holder
